# Fritzing sketch Sketch (saved by Fritzing 0.9.5d)

parts:
  Part1 = Arduino Uno (Rev3)
  DHT1 = DHT22 Humidity and Temperature Sensor
  Grove1 = Grove OLED 128x96

nets:
  N1: Part1.A4/SDA, Grove1.SDA
  N2: Part1.A5/SCL, Grove1.SCL
  N3: Part1.D2, DHT1.DATA
  5V: Part1.5V, DHT1.VDD, Grove1.VCC
  GND: Part1.GND, DHT1.GND, Grove1.GND
